# Fritzing sketch schematic (saved by Fritzing 0.9.3b)
breadboards: 1

parts:
  part = IC, SIP package, 8 pins
  Raspberry_Pi_3 = Raspberry Pi 3
  part_2 = IC, SIP package, 5 pins
  part_3 = IC, SIP package, 5 pins
  part_4 = IC, SIP package, 7 pins

nets:
  3V3: part.pin1, Raspberry_Pi_3.3v3, Raspberry_Pi_3.3V3, part_2.pin4, part_3.pin4
  N1: part.pin2, Raspberry_Pi_3.5V, part_4.pin6
  N2: part.pin3, part.pin4, Raspberry_Pi_3.GND, part_2.pin5, part_3.pin5, part_4.pin7
  N3: part.pin5, Raspberry_Pi_3.GPIO18
  N4: part.pin6, Raspberry_Pi_3.GPIO19
  N5: part.pin7, Raspberry_Pi_3.GPIO20
  N6: part.pin8, Raspberry_Pi_3.GPIO21
  N7: Raspberry_Pi_3.GPIO17, part_3.pin2
  N8: Raspberry_Pi_3.GPIO27, part_3.pin1
  N9: Raspberry_Pi_3.GPIO10, part_4.pin1
  N10: Raspberry_Pi_3.GPIO11, part_4.pin2
  N11: Raspberry_Pi_3.GPIO5, part_2.pin1
  N12: Raspberry_Pi_3.GPIO6, part_2.pin2
  N13: Raspberry_Pi_3.GPIO13, part_2.pin3
  N14: Raspberry_Pi_3.GPIO26, part_3.pin3
  N15: Raspberry_Pi_3.GPIO8, part_4.pin5
  N16: Raspberry_Pi_3.GPIO25, part_4.pin4
  N17: Raspberry_Pi_3.GPIO24, part_4.pin3

notes:
  MiniAmp
  Frequency
  Volume
  OLED
